# Fritzing sketch breadboard (saved by Fritzing 0.9.10b)
breadboards: 1

parts:
  Bauteil1 = Arduino Uno (Rev3)
  S1 = Pushbutton [package="[THT]"]
  S2 = Pushbutton [package="[THT]"]
  S3 = Pushbutton [package="[THT]"]
  R1 = Resistor [tolerance=±5% resistance=10k package="2512 [SMD]"]
  R2 = Resistor [tolerance=±5% resistance=10k package="2512 [SMD]"]
  R3 = Resistor [tolerance=±5% resistance=10k package="2512 [SMD]"]
  LED1 = LED - 5mm [color="Blue (430nm)" current=0.030 package="5 mm [THT]"]
  LED2 = LED - 5mm [color="Yellow (585nm)" current=0.030 package="5 mm [THT]"]
  LED3 = LED - 5mm [color="Red (635nm)" current=0.030 package="5 mm [THT]"]
  R4 = Resistor [tolerance=±5% resistance=10k package="2512 [SMD]"]
  SG1 = Buzzer 12mm [package=buzzer-ccv-kit]

nets:
  N1: Bauteil1.D8, SG1.2
  N2: Bauteil1.GND, R1.Pin_1, R2.Pin_1, R3.Pin_1, R4.Pin_1, SG1.1
  N3: Bauteil1.D2, S1.Pin_1, S1.Pin_2, R3.Pin_0
  N4: Bauteil1.D3_PWM, S2.Pin_1, S2.Pin_2, R2.Pin_0
  N5: Bauteil1.D4, S3.Pin_1, S3.Pin_2, R1.Pin_0
  N6: Bauteil1.D5_PWM, LED1.anode
  N7: Bauteil1.D6_PWM, LED2.anode
  N8: Bauteil1.D7, LED3.anode
  N9: Bauteil1.3V3, S1.Pin_3, S1.Pin_4, S2.Pin_3, S2.Pin_4, S3.Pin_3, S3.Pin_4
  N10: LED1.cathode, LED2.cathode, LED3.cathode, R4.Pin_0
